# Fritzing sketch RescueAVR-megaX8 (saved by Fritzing 0.8.3b)
breadboards: 1

parts:
  R1 = Resistor [tolerance=±5% resistance=4.7k package=THT]
  R2 = Resistor [tolerance=±5% resistance=1k package=THT]
  R3 = Resistor [tolerance=±5% resistance=100 package=THT]
  R4 = Resistor [tolerance=±5% resistance=1k package=THT]
  R5 = Resistor [tolerance=±10% resistance=10k package=THT]
  +12V = Screw terminal - 2 pins [package=THT]
  Bauteil1 = Arduino Uno (Rev3)
  BC547_-_NPN_(CBE) = NPN-Transistor [package="TO92 [THT]"]
  BC557_-_PNP_(CBE) = PNP-Transistor [package="TO92 [THT]"]
  U1 = atmega328 [package=dip]

nets:
  N1: R1.Pin_0, BC547_-_NPN_(CBE).B
  N2: R1.Pin_1, Bauteil1.ICSP_SCK, Bauteil1.D13/SCK
  N3: R2.Pin_0, R5.Pin_1, BC557_-_PNP_(CBE).B
  N4: R2.Pin_1, BC547_-_NPN_(CBE).C
  N5: R3.Pin_1, R4.Pin_0, BC557_-_PNP_(CBE).C
  GND: R4.Pin_1, +12V.pin2, Bauteil1.GND, BC547_-_NPN_(CBE).E, U1.GND, U1.D7
  N6: R5.Pin_0, +12V.+12Volt, BC557_-_PNP_(CBE).E
  N7: Bauteil1.A0, U1.XLAT1
  N8: Bauteil1.A1, U1.D4
  N9: Bauteil1.A2, U1.D3_(PWM)
  N10: Bauteil1.A3, U1.D2
  N11: Bauteil1.A4/SDA, U1.D1_(TX)
  N12: Bauteil1.A5/SCL, U1.A2
  N13: Bauteil1.ICSP_MISO, Bauteil1.D12/MISO, U1.VCC, U1.AVCC
  N14: Bauteil1.ICSP_MOSI, Bauteil1.D11_PWM/MOSI, U1.D6_(PWM)
  N15: Bauteil1.D8, U1.D9_(PWM)
  N16: Bauteil1.D9_PWM, U1.D8
  N17: Bauteil1.D10_PWM/SS, U1.D5_(PWM)
  N18: Bauteil1.D2, U1.A1
  N19: Bauteil1.D3_PWM, U1.A0
  N20: Bauteil1.D4, U1.D13
  N21: Bauteil1.D5_PWM, U1.D12
  N22: Bauteil1.D6_PWM, U1.D11_(PWM)
  N23: Bauteil1.D7, U1.D10_(PWM)

notes:
  HVPP-pin mapping
  ATmegaX8 Arduino
  Pin Function
  1 RESET 12V
  2 N.C.
  3 ‎RDY A4
  4 OEi A3
  5 WRi A2
  6 BS1 A1
  7 Vcc 12
  8 GND
  9 XTAL1 A0
  10 N.C.
  11 XA0 10
  12 XA1 11
  13 PAGEL->GND
  14 DATA0 9
  15 DATA1 8
  16 DATA2 7
  17 DATA3 6
  18 DATA4 5
  19 DATA5 4
  20 Vcc 12
  21 N.C.
  22 GND
  23 DATA6 3
  24 DATA7 2
  25 BS2 A5
  26 N.C.
  27 N.C.
  28 N.C.

custom parts:
  Screw terminal - 2 pins: Screw terminal with 2 pins
