# Fritzing sketch RescueAVR-tinyX4 (saved by Fritzing 0.8.3b)
breadboards: 1

parts:
  R1 = Resistor [tolerance=±5% resistance=4.7k package=THT]
  R2 = Resistor [tolerance=±5% resistance=1k package=THT]
  R3 = Resistor [tolerance=±5% resistance=100 package=THT]
  R4 = Resistor [tolerance=±5% resistance=1k package=THT]
  R5 = Resistor [tolerance=±10% resistance=10k package=THT]
  +12V = Screw terminal - 2 pins [package=THT]
  Bauteil1 = Arduino Uno (Rev3)
  BC547_-_NPN_(CBE) = NPN-Transistor [package="TO92 [THT]"]
  BC557_-_PNP_(CBE) = PNP-Transistor [package="TO92 [THT]"]
  U1 = ATtinyX4 [package="DIP8 [THT]"]

nets:
  N1: R1.Pin_0, BC547_-_NPN_(CBE).B
  N2: R1.Pin_1, Bauteil1.ICSP_SCK, Bauteil1.D13/SCK
  N3: R2.Pin_0, R5.Pin_1, BC557_-_PNP_(CBE).B
  N4: R2.Pin_1, BC547_-_NPN_(CBE).C
  N5: R3.Pin_1, R4.Pin_0, BC557_-_PNP_(CBE).C
  GND: R4.Pin_1, +12V.pin2, Bauteil1.GND, BC547_-_NPN_(CBE).E, U1.PA2, U1.PA1, U1.PA0, U1.GND
  N6: R5.Pin_0, +12V.+12Volt, BC557_-_PNP_(CBE).E
  N7: Bauteil1.A0, U1.PA6
  N8: Bauteil1.A1, U1.PA5
  N9: Bauteil1.A2, U1.PA4
  N10: Bauteil1.A5/SCL, U1.PB0
  N11: Bauteil1.ICSP_MISO, Bauteil1.D12/MISO, U1.VCC

notes:
  HVSP-pin mapping
  ATtinyX4 Arduino
  Pin Function
  1 Vcc 12
  2 SCI A5
  3 N.C.
  4 RESET 12V
  5 N.C.
  6 N.C.
  7 SDI A0
  8 SII A1
  9 SDO A2
  10 N.C.
  11 GND
  12 GND
  13 GND
  14 GND

custom parts:
  Screw terminal - 2 pins: Screw terminal with 2 pins
  ATtinyX4: The high-performance, low-power Atmel 8-bit AVR RISC-based microcontroller combines 8KB ISP flash memory, 512B EEPROM, 512-Byte SRAM, 12 general purpose I/O lines, 32 general purpose working registers, an 2 timers/counters (8-bit/16-bit) with two PWM channels each, internal and external interrupts, 8-channel 10-bit A/D converter, programmable gain stage (1x, 20x) for 12 differential ADC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
