# Fritzing sketch RescueAVR-tinyX5 (saved by Fritzing 0.8.3b)
breadboards: 1

parts:
  R1 = Resistor [tolerance=±5% resistance=4.7k package=THT]
  R2 = Resistor [tolerance=±5% resistance=1k package=THT]
  R3 = Resistor [tolerance=±5% resistance=100 package=THT]
  R4 = Resistor [tolerance=±5% resistance=1k package=THT]
  R5 = Resistor [tolerance=±10% resistance=10k package=THT]
  +12V = Screw terminal - 2 pins [package=THT]
  Bauteil1 = Arduino Uno (Rev3)
  BC547_-_NPN_(CBE) = NPN-Transistor [package="TO92 [THT]"]
  BC557_-_PNP_(CBE) = PNP-Transistor [package="TO92 [THT]"]
  U1 = attiny85 [package=dip]

nets:
  N1: R1.Pin_0, BC547_-_NPN_(CBE).B
  N2: R1.Pin_1, Bauteil1.ICSP_SCK, Bauteil1.D13/SCK
  N3: R2.Pin_0, R5.Pin_1, BC557_-_PNP_(CBE).B
  N4: R2.Pin_1, BC547_-_NPN_(CBE).C
  N5: R3.Pin_0, U1.Pin_1
  N6: R3.Pin_1, R4.Pin_0, BC557_-_PNP_(CBE).C
  N7: R4.Pin_1, +12V.pin2, Bauteil1.GND, BC547_-_NPN_(CBE).E, U1.Pin_4
  N8: R5.Pin_0, +12V.+12Volt, BC557_-_PNP_(CBE).E
  N9: Bauteil1.A0, U1.Pin_5
  N10: Bauteil1.A1, U1.Pin_6
  N11: Bauteil1.A2, U1.Pin_7
  N12: Bauteil1.A5/SCL, U1.Pin_2
  N13: Bauteil1.ICSP_MISO, Bauteil1.D12/MISO, U1.Pin_8

notes:
  HVSP-pin mapping
  ATtinyX5 Arduino
  Pin Function
  1 RESET 12V
  2 SCI A5
  3 N.C.
  4 N.C.
  5 SDI A0
  6 SII A1
  7 SDO A2
  8 Vcc 12

custom parts:
  Screw terminal - 2 pins: Screw terminal with 2 pins
